// Logisim project LC-2200-16.circ as structural Verilog: 2 circuits, main circuit main
module main (
);

  wire ALUHi, ALULo, clock, comparator_1_eq, comparator_2_eq, DrALU, DrMEM, DrOFF, DrPC, DrREG, LdA, LdB,
       LdIR, LdMAR, LdPC, LdZ, not_1_out, RegSelHi, RegSelLo, WrMEM, WrREG, Z;
  wire [1:0] bit_extender_1_out, CTRLCD;
  wire [2:0] opcode;
  wire [3:0] regno, RX, RY;
  wire [3:1] RZ;
  wire [5:0] multiplexer_3_out, rom_2_data, rom_3_data, State_q;
  wire [15:0] A_q, ALU_output, B_q, bit_extender_2_out, controlled_buffer_1_out, MAR_q, multiplexer_2_out,
       PC_q, ram_1_data, ram_2_data;
  wire [24:0] rom_1_data;

  Clock clock_1 (.out(clock));
  Register #(.width(16)) PC (.D(controlled_buffer_1_out), .en(LdPC), .Q(PC_q), .clk(clock));  // open: clr
  assign controlled_buffer_1_out = DrPC ? PC_q : 16'bz;  // Controlled_Buffer controlled_buffer_1
  Multiplexer #(.select(2), .width(4), .enable("false")) multiplexer_1 (
    .in0(RX), .in1(RY), .in2({RZ, CTRLCD[1]}), .out(regno), .sel({RegSelHi, RegSelLo}));  // open: in3
  Register #(.width(16)) A (.D(controlled_buffer_1_out), .en(LdA), .Q(A_q), .clk(clock));  // open: clr
  Comparator #(.width(16)) comparator_1 (
    .a(controlled_buffer_1_out), .b({16{1'b0}}), .eq(comparator_1_eq));  // open: gt, lt
  Register #(.width(16)) B (.D(controlled_buffer_1_out), .en(LdB), .Q(B_q), .clk(clock));  // open: clr
  ALU ALU (.func({ALUHi, ALULo}), .A(A_q), .B(B_q), .Output(ALU_output));
  assign controlled_buffer_1_out = DrALU ? ALU_output : 16'bz;  // Controlled_Buffer controlled_buffer_2
  Register #(.width(1)) register_1 (.D(comparator_1_eq), .en(LdZ), .Q(Z), .clk(clock));  // open: clr
  assign bit_extender_1_out = {{1{1'b0}}, Z};  // Bit_Extender bit_extender_1
  Comparator #(.width(4)) comparator_2 (.a(regno), .b(4'b0000), .eq(comparator_2_eq));  // open: gt, lt
  RAM #(.addrWidth(4), .dataWidth(16), .bus("separate")) ram_1 (
    .addr(regno), .din(controlled_buffer_1_out), .data(ram_1_data), .str(WrREG), .clk(clock), .ld(1'b1));  // open: sel, clr
  not not_1 (not_1_out, comparator_2_eq);
  Multiplexer #(.width(16), .enable("false")) multiplexer_2 (
    .in0({16{1'b0}}), .in1(ram_1_data), .out(multiplexer_2_out), .sel(not_1_out));
  assign controlled_buffer_1_out = DrREG ? multiplexer_2_out : 16'bz;  // Controlled_Buffer controlled_buffer_3
  ROM #(.addrWidth(6), .dataWidth(25)) rom_1 (
    .addr(State_q),
    .data({rom_1_data[24:23], ALUHi, ALULo, RegSelHi, RegSelLo, WrMEM, WrREG, LdZ, LdB, LdA, LdMAR, LdIR, LdPC, DrOFF, DrPC, DrALU, DrMEM, DrREG, rom_1_data[5:0]}));  // open: sel
  ROM #(.addrWidth(3), .dataWidth(6)) rom_2 (.addr(opcode), .data(rom_2_data));  // open: sel
  ROM #(.addrWidth(2), .dataWidth(6)) rom_3 (.addr(bit_extender_1_out), .data(rom_3_data));  // open: sel
  Register #(.width(16)) MAR (.D(controlled_buffer_1_out), .en(LdMAR), .Q(MAR_q), .clk(clock));  // open: clr
  Multiplexer #(.select(2), .width(6), .enable("false")) multiplexer_3 (
    .in0(rom_1_data[5:0]), .in1(rom_2_data), .in2(rom_3_data), .out(multiplexer_3_out),
    .sel(rom_1_data[24:23]));  // open: in3
  Register #(.width(16)) IR (
    .D(controlled_buffer_1_out), .en(LdIR), .Q({opcode, RX, RY, RZ, CTRLCD}), .clk(clock));  // open: clr
  RAM #(.addrWidth(16), .dataWidth(16), .bus("separate")) ram_2 (
    .addr(MAR_q), .din(controlled_buffer_1_out), .data(ram_2_data), .str(WrMEM), .clk(clock), .ld(1'b1));  // open: sel, clr
  assign controlled_buffer_1_out = DrMEM ? ram_2_data : 16'bz;  // Controlled_Buffer controlled_buffer_4
  Register #(.width(6)) State (.D(multiplexer_3_out), .en(1'b1), .Q(State_q), .clk(clock));  // open: clr
  assign bit_extender_2_out = {{11{RZ[3]}}, {RZ, CTRLCD}};  // Bit_Extender bit_extender_2
  assign controlled_buffer_1_out = DrOFF ? bit_extender_2_out : 16'bz;  // Controlled_Buffer controlled_buffer_5

  // Other names for the same wires on the sheet: func[1:0] = {ALUHi, ALULo}; RZ[0] = CTRLCD[1]

  // Notes on the sheet:
  //   contents of rom_1 (hex, n*v repeats v):
  //   6201 1082 e00900 84044 108045 20100 84047 108048 220100 8404a 840b 20100 8404d 840e 210f 20080 84051
  //   8412 2113 40040 84055 8056 410117 1004200 8419 900 a021b 840 1c
  //   contents of rom_2 (hex, n*v repeats v):
  //   3 6 9 c 10 14 1a 1c
  //   contents of rom_3 (hex, n*v repeats v):
  //   0 18
endmodule

module ALU (
  input  [15:0] A,
  input  [15:0] B,
  input  [1:0] func,
  output [15:0] Output
);

  wire [15:0] adder_1_out, adder_2_out, nand_1_out, subtractor_1_out;

  Subtractor #(.width(16)) subtractor_1 (.a(A), .b(B), .out(subtractor_1_out));  // open: bin, bout
  assign nand_1_out = ~(A & B);  // NAND_Gate nand_1, 16 bits wide
  Adder #(.width(16)) adder_1 (.a(A), .b(B), .out(adder_1_out));  // open: cin, cout
  Adder #(.width(16)) adder_2 (.a(16'h1), .b(A), .out(adder_2_out));  // open: cin, cout
  Multiplexer #(.select(2), .width(16)) multiplexer_1 (
    .in0(adder_1_out), .in1(nand_1_out), .in2(subtractor_1_out), .in3(adder_2_out), .out(Output), .sel(func),
    .en(1'b1));
endmodule
